// Logisim project projeto.circ as structural Verilog: 14 circuits, main circuit main
module main (
  input  in_1,
  input  Jogador__0,
  input  in_3,
  input  in_4,
  input  in_5,
  input  Jogador__1,
  input  in_7,
  input  in_8,
  input  Jogador,
  input  Confirmar
);

  wire button_1_out, decode_2_a, decode_2_b, decode_2_c, decode_2_d, decode_2_e, decode_2_f, decode_2_g,
       decode_a, decode_b, decode_c, decode_d, decode_e, decode_f, decode_g, game_out_6, game_out_7,
       game_out_8;
  wire [3:0] Random_out_2;

  _7_Segment_Display u_7_segment_display_1 (
    .g(decode_g), .f(decode_f), .a(decode_a), .b(decode_b), .e(decode_e), .d(decode_d), .c(decode_c));  // open: dp
  _7_Segment_Display u_7_segment_display_2 (
    .g(decode_2_g), .f(decode_2_f), .a(decode_2_a), .b(decode_2_b), .e(decode_2_e), .d(decode_2_d),
    .c(decode_2_c));  // open: dp
  decode decode (
    .in_1({in_1, Jogador__0, in_3, in_4}), .G(decode_g), .F(decode_f), .E(decode_e), .D(decode_d),
    .C(decode_c), .B(decode_b), .A(decode_a));
  decode decode_2 (
    .in_1({in_5, Jogador__1, in_7, in_8}), .G(decode_2_g), .F(decode_2_f), .E(decode_2_e), .D(decode_2_d),
    .C(decode_2_c), .B(decode_2_b), .A(decode_2_a));
  Button button_1 (.out(button_1_out));
  random Random (.out_2(Random_out_2), .in_1(button_1_out));
  game game (
    .J0({in_1, Jogador__0, in_3, in_4}), .J1({in_5, Jogador__1, in_7, in_8}), .Jogador(Jogador),
    .Confirmar(Confirmar), .out_6(game_out_6), .out_7(game_out_7), .out_8(game_out_8), .valor(Random_out_2));
  LED led_1 (.in(game_out_6));
  LED led_2 (.in(game_out_7));
  LED led_3 (.in(game_out_8));

  // Notes on the sheet:
  //   =
  //   <
  //   >
endmodule

module game (
  input  [3:0] J0,
  input  [3:0] J1,
  input  [3:0] valor,
  input  Jogador,
  input  Confirmar,
  output out_6,
  output out_7,
  output out_8
);

  wire Mag_out_3, Mag_out_4, Mag_out_5;
  wire [3:0] Mux_out_4;

  mux Mux (.J0(J0), .J1(J1), .Jogador(Jogador), .out_4(Mux_out_4));
  magnitute Mag (.in_1(Mux_out_4), .in_2(valor), .out_3(Mag_out_3), .out_4(Mag_out_4), .out_5(Mag_out_5));
  and and_1 (out_6, Mag_out_3, Confirmar);
  and and_2 (out_7, Mag_out_4, Confirmar);
  and and_3 (out_8, Mag_out_5, Confirmar);

  // Notes on the sheet:
  //   >
  //   =
  //   <
endmodule

module random (
  input  in_1,
  output [3:0] out_2
);

  Random #(.width(4)) random_1 (.clk(in_1), .next(in_1), .out(out_2));  // open: clr
endmodule

module mux (
  input  [3:0] J0,
  input  [3:0] J1,
  input  Jogador,
  output [3:0] out_4
);

  wire [3:0] and_1_out, and_2_out;

  assign and_1_out = J0 & ~{4{Jogador}};  // AND_Gate and_1, 4 bits wide
  assign and_2_out = J1 & {4{Jogador}};  // AND_Gate and_2, 4 bits wide
  assign out_4 = and_1_out | and_2_out;  // OR_Gate or_1, 4 bits wide
endmodule

module magnitute (
  input  [3:0] in_1,
  input  [3:0] in_2,
  output out_3,
  output out_4,
  output out_5
);

  wire and_1_out, and_2_out, and_3_out, and_4_out, xnor_1_out, xnor_2_out, xnor_3_out, xnor_4_out;

  xnor xnor_1 (xnor_1_out, in_1[0], in_2[0]);
  xnor xnor_2 (xnor_2_out, in_1[1], in_2[1]);
  xnor xnor_3 (xnor_3_out, in_1[2], in_2[2]);
  xnor xnor_4 (xnor_4_out, in_1[3], in_2[3]);
  and and_1 (and_1_out, in_1[3], ~in_2[3]);  // AND_Gate
  and and_2 (and_2_out, xnor_4_out, in_1[2], ~in_2[2]);  // AND_Gate
  and and_3 (and_3_out, xnor_4_out, xnor_3_out, in_1[1], ~in_2[1]);  // AND_Gate
  and and_4 (and_4_out, xnor_4_out, xnor_3_out, xnor_2_out, in_1[0], ~in_2[0]);  // AND_Gate
  and and_5 (out_3, xnor_1_out, xnor_2_out, xnor_3_out, xnor_4_out);
  or \or  (out_4, and_1_out, and_2_out, and_3_out, and_4_out);
  and and_6 (out_5, ~out_3, ~out_4);  // AND_Gate
endmodule

module decode (
  input  [3:0] in_1,
  output G,
  output F,
  output E,
  output D,
  output C,
  output B,
  output A
);

  Seg_G seg_g_1 (.in_1(in_1), .out_2(G));
  Seg_F seg_f_1 (.in_1(in_1), .out_2(F));
  Seg_E seg_e_1 (.in_1(in_1), .out_2(E));
  Seg_D seg_d_1 (.in_1(in_1), .out_2(D));
  Seg_C seg_c_1 (.in_1(in_1), .out_2(C));
  Seg_B seg_b_1 (.in_1(in_1), .out_2(B));
  Seg_A seg_a_1 (.in_1(in_1), .out_2(A));
endmodule

module Seg_A (
  input  [3:0] in_1,
  output out_2
);

  wire and_1_out, and_2_out, and_3_out, and_4_out, and_5_out, and_6_out, and_7_out;

  and and_1 (and_1_out, ~in_1[3], in_1[1]);  // AND_Gate
  and and_2 (and_2_out, in_1[2], in_1[1]);
  and and_3 (and_3_out, in_1[3], in_1[1], ~in_1[0]);  // AND_Gate
  and and_4 (and_4_out, in_1[3], ~in_1[2], ~in_1[1]);  // AND_Gate
  and and_5 (and_5_out, in_1[3], ~in_1[1], ~in_1[0]);  // AND_Gate
  and and_6 (and_6_out, ~in_1[3], in_1[2], in_1[0]);  // AND_Gate
  and and_7 (and_7_out, ~in_1[3], ~in_1[2], ~in_1[0]);  // AND_Gate
  or or_1 (out_2, and_1_out, and_2_out, and_3_out, and_4_out, and_5_out, and_6_out, and_7_out);
endmodule

module Seg_B (
  input  [3:0] in_1,
  output out_2
);

  wire and_1_out, and_2_out, and_3_out, and_4_out, and_5_out;

  and and_1 (and_1_out, ~in_1[3], ~in_1[2]);  // AND_Gate
  and and_2 (and_2_out, ~in_1[3], ~in_1[1], ~in_1[0]);  // AND_Gate
  and and_3 (and_3_out, ~in_1[3], in_1[1], in_1[0]);  // AND_Gate
  and and_4 (and_4_out, in_1[3], ~in_1[1], in_1[0]);  // AND_Gate
  and and_5 (and_5_out, in_1[3], ~in_1[2], ~in_1[0]);  // AND_Gate
  or or_1 (out_2, and_1_out, and_2_out, and_3_out, and_4_out, and_5_out);
endmodule

module Seg_C (
  input  [3:0] in_1,
  output out_2
);

  wire and_1_out, and_2_out, and_3_out, and_4_out, and_5_out;

  and and_1 (and_1_out, ~in_1[3], ~in_1[1]);  // AND_Gate
  and and_2 (and_2_out, in_1[3], ~in_1[2]);  // AND_Gate
  and and_3 (and_3_out, ~in_1[3], in_1[2], in_1[1]);  // AND_Gate
  and and_4 (and_4_out, in_1[3], ~in_1[1], in_1[0]);  // AND_Gate
  and and_5 (and_5_out, ~in_1[3], in_1[1], in_1[0]);  // AND_Gate
  or or_1 (out_2, and_1_out, and_2_out, and_3_out, and_4_out, and_5_out);
endmodule

module Seg_D (
  input  [3:0] in_1,
  output out_2
);

  wire and_1_out, and_2_out, and_3_out, and_4_out, and_5_out, and_6_out;

  and and_1 (and_1_out, in_1[3], ~in_1[1]);  // AND_Gate
  and and_2 (and_2_out, ~in_1[3], ~in_1[2], in_1[1]);  // AND_Gate
  and and_3 (and_3_out, in_1[2], ~in_1[1], in_1[0]);  // AND_Gate
  and and_4 (and_4_out, in_1[2], in_1[1], ~in_1[0]);  // AND_Gate
  and and_5 (and_5_out, in_1[3], ~in_1[2], in_1[0]);  // AND_Gate
  and and_6 (and_6_out, ~in_1[3], ~in_1[2], ~in_1[0]);  // AND_Gate
  or or_1 (out_2, and_1_out, and_2_out, and_3_out, and_4_out, and_5_out, and_6_out);
endmodule

module Seg_E (
  input  [3:0] in_1,
  output out_2
);

  wire and_1_out, and_2_out, and_3_out, and_4_out;

  and and_1 (and_1_out, in_1[3], in_1[2]);
  and and_2 (and_2_out, in_1[1], ~in_1[0]);  // AND_Gate
  and and_3 (and_3_out, in_1[3], in_1[1], in_1[0]);
  and and_4 (and_4_out, ~in_1[2], ~in_1[1], ~in_1[0]);  // AND_Gate
  or or_1 (out_2, and_1_out, and_2_out, and_3_out, and_4_out);
endmodule

module Seg_F (
  input  [3:0] in_1,
  output out_2
);

  wire and_1_out, and_2_out, and_3_out, and_4_out, and_5_out;

  and and_1 (and_1_out, in_1[3], in_1[1]);
  and and_2 (and_2_out, ~in_1[1], ~in_1[0]);  // AND_Gate
  and and_3 (and_3_out, in_1[3], ~in_1[2], ~in_1[1]);  // AND_Gate
  and and_4 (and_4_out, ~in_1[3], in_1[2], ~in_1[1]);  // AND_Gate
  and and_5 (and_5_out, ~in_1[3], in_1[2], ~in_1[0]);  // AND_Gate
  or or_1 (out_2, and_1_out, and_2_out, and_3_out, and_4_out, and_5_out);
endmodule

module Seg_G (
  input  [3:0] in_1,
  output out_2
);

  wire and_1_out, and_2_out, and_3_out, and_4_out, and_5_out;

  and and_1 (and_1_out, in_1[1], ~in_1[0]);  // AND_Gate
  and and_2 (and_2_out, in_1[3], in_1[0]);
  and and_3 (and_3_out, ~in_1[3], in_1[2], ~in_1[1]);  // AND_Gate
  and and_4 (and_4_out, in_1[3], ~in_1[2], ~in_1[1]);  // AND_Gate
  and and_5 (and_5_out, ~in_1[3], ~in_1[2], in_1[1]);  // AND_Gate
  or or_1 (out_2, and_1_out, and_2_out, and_3_out, and_4_out, and_5_out);
endmodule

module teste (
  input  [3:0] in_1,
  output out_2
);

  wire magnitute_1_out_3, magnitute_2_out_3, magnitute_3_out_3, magnitute_4_out_3, magnitute_5_out_3,
       magnitute_6_out_3, magnitute_7_out_3, magnitute_8_out_3, magnitute_9_out_3, magnitute_10_out_3;

  magnitute magnitute_1 (.in_1(in_1), .in_2(4'b0100), .out_3(magnitute_1_out_3));  // open: out_4, out_5
  magnitute magnitute_2 (.in_1(in_1), .in_2(4'b0000), .out_3(magnitute_2_out_3));  // open: out_4, out_5
  magnitute magnitute_3 (.in_1(in_1), .in_2(4'b0001), .out_3(magnitute_3_out_3));  // open: out_4, out_5
  magnitute magnitute_4 (.in_1(in_1), .in_2(4'b0010), .out_3(magnitute_4_out_3));  // open: out_4, out_5
  magnitute magnitute_5 (.in_1(in_1), .in_2(4'b0011), .out_3(magnitute_5_out_3));  // open: out_4, out_5
  magnitute magnitute_6 (.in_1(in_1), .in_2(4'b0111), .out_3(magnitute_6_out_3));  // open: out_4, out_5
  magnitute magnitute_7 (.in_1(in_1), .in_2(4'b1000), .out_3(magnitute_7_out_3));  // open: out_4, out_5
  magnitute magnitute_8 (.in_1(in_1), .in_2(4'b1001), .out_3(magnitute_8_out_3));  // open: out_4, out_5
  magnitute magnitute_9 (.in_1(in_1), .in_2(4'b1010), .out_3(magnitute_9_out_3));  // open: out_4, out_5
  magnitute magnitute_10 (.in_1(in_1), .in_2(4'b1101), .out_3(magnitute_10_out_3));  // open: out_4, out_5
  or or_1 (out_2, magnitute_2_out_3, magnitute_3_out_3, magnitute_4_out_3, magnitute_5_out_3, magnitute_1_out_3, magnitute_6_out_3, magnitute_7_out_3, magnitute_8_out_3, magnitute_9_out_3, magnitute_10_out_3);
endmodule
