// Logisim project projeto-2.circ as structural Verilog: 24 circuits, main circuit main
module main (
  input  in_1,
  input  in_2,
  input  in_3,
  input  in_4,
  input  in_5,
  input  in_6,
  input  in_7,
  input  in_8
);

  wire A_ganhou, A_JOGANDO, acertou, and_1_out, and_5_out, and_10_out, and_11_out, and_12_out, and_13_out,
       and_14_out, and_18_out, B_ganhou, B_JOGANDO, certo, CHUTANDO_X, CHUTANDO_Y, CHUTAR, configurar,
       d_ff_2_qn, d_ff_3_qn, d_ff_4_qn, debugger_random_1_out_2, dm, dma_t, dmb_t, ds, dsa_t, dsb_t, Empate,
       Fim_de_jogo, fim_temp_1_out_5, fim_temp_2_out_5, igual, Iniciar, mag_inteiro_1_igual,
       mag_inteiro_1_maior, mag_inteiro_1_menor, mag_inteiro_2_igual, mag_inteiro_3_igual, magnitute_1_out_3,
       magnitute_1_out_4, magnitute_1_out_5, maior, menor, multiplexer_2_out, not_1_out, not_2_out,
       not_3_out, not_4_out, not_5_out, not_6_out, ok, or_1_out, or_3_out, or_7_out, p2, pont_max_1_out_2,
       pont_max_2_out_2, PROXIMO, reset, running, SA, SB, \situação_1_out_4 , SValSomChute, SValSomGuess,
       SVX, SVY, SX, SY, time_1_out_2, time_2_out_2, troca, tunnel, um, uma_t, umb_t, undriven, undriven_2,
       us, usa_t, usb_t;
  wire [2:0] random_2_out, random_4_out;
  wire [3:0] DMA, DMB, DSA, DSB, GA, GB, multiplexer_1_out, PA, PB, UMA, UMB, USA, USB, valSomChute,
       valSomGuess, ValX, ValY, XHC, YHC;

  magnitute magnitute_1 (
    .in_1(PA), .in_2(PB), .out_3(magnitute_1_out_3), .out_4(magnitute_1_out_4), .out_5(magnitute_1_out_5));
  and and_1 (and_1_out, CHUTANDO_Y, PROXIMO);
  \time  time_1 (.in_1(and_1_out), .out_2(time_1_out_2));
  mag_inteiro mag_inteiro_1 (
    .in_1(SValSomChute), .in_2(valSomChute), .in_3(SValSomGuess), .in_4(valSomGuess),
    .Igual(mag_inteiro_1_igual), .maior(mag_inteiro_1_maior), .menor(mag_inteiro_1_menor));  // open: positivo, negativo
  mag_inteiro mag_inteiro_2 (
    .in_1(SVX), .in_2(ValX), .in_3(SX), .in_4(XHC), .Igual(mag_inteiro_2_igual));  // open: maior, menor, positivo, negativo
  mag_inteiro mag_inteiro_3 (
    .in_1(SVY), .in_2(ValY), .in_3(SY), .in_4(YHC), .Igual(mag_inteiro_3_igual));  // open: maior, menor, positivo, negativo
  and and_2 (Empate, magnitute_1_out_3, Fim_de_jogo);
  and and_3 (A_ganhou, magnitute_1_out_4, Fim_de_jogo);
  and and_4 (B_ganhou, magnitute_1_out_5, Fim_de_jogo);
  and and_5 (and_5_out, PROXIMO, time_1_out_2);
  and and_6 (igual, ok, mag_inteiro_1_igual);
  and and_7 (maior, ok, mag_inteiro_1_maior);
  and and_8 (menor, ok, mag_inteiro_1_menor);
  and and_9 (certo, mag_inteiro_2_igual, ok, mag_inteiro_3_igual);
  D_Flip_Flop #(.Pre_Clr_Positions("LEGACY"), .enable("true"), .NewFFLayout("false")) d_ff_1 (
    .clk(certo), .D(certo), .Q(acertou), .reset(not_1_out));  // open: Qn, preset, en
  not not_1 (not_1_out, ok);
  and and_10 (and_10_out, certo, CHUTANDO_Y, ok, A_JOGANDO);
  incrementa incrementa_1 (.in_1(and_10_out), .reset(reset), .out_3(PA));
  incrementa incrementa_2 (.in_1(and_11_out), .reset(reset), .out_3(PB));
  and and_11 (and_11_out, certo, CHUTANDO_Y, ok, B_JOGANDO);
  Button button_1 (.out(uma_t));
  Button button_2 (.out(dma_t));
  Hex_Digit_Display hex_digit_display_1 (.value(DMA));  // open: dp
  Hex_Digit_Display hex_digit_display_2 (.value(UMA));  // open: dp
  _7_Segment_Display u_7_segment_display_1 (
    .g(SA), .f(not_2_out), .a(not_2_out), .b(not_2_out), .e(not_2_out), .d(not_2_out), .c(not_2_out));  // open: dp
  or or_1 (or_1_out, troca, and_5_out);
  Button button_3 (.out(dsa_t));
  LED led_1 (.in(undriven));
  LED led_2 (.in(undriven));
  Hex_Digit_Display hex_digit_display_3 (.value(DSA));  // open: dp
  Hex_Digit_Display hex_digit_display_4 (.value(PA));  // open: dp
  not not_2 (not_2_out, SA);
  Hex_Digit_Display hex_digit_display_5 (.value(GA));  // open: dp
  LED led_3 (.in(A_JOGANDO));
  not not_3 (not_3_out, p2);
  \situação  \situação_1  (.in_1(PROXIMO), .in_2(CHUTANDO_Y), .ok(ok), .out_4(\situação_1_out_4 ));
  fim_temp fim_temp_1 (.in_1(DMA), .in_2(UMA), .in_3(DSA), .in_4(USA), .out_5(fim_temp_1_out_5));
  fim_temp fim_temp_2 (.in_1(DMB), .in_2(UMB), .in_3(DSB), .in_4(USB), .out_5(fim_temp_2_out_5));
  pont_max pont_max_1 (.in_1(PA), .out_2(pont_max_1_out_2));
  pont_max pont_max_2 (.in_1(PB), .out_2(pont_max_2_out_2));
  Button button_4 (.out(usa_t));
  Hex_Digit_Display hex_digit_display_6 (.value(USA));  // open: dp
  cronometro_p1 cronometro_p1_1 (
    .proximo(or_1_out), .START(Iniciar), .DMP(dm), .UMP(um), .CONFIG(configurar), .DM(DMA), .UM(UMA),
    .DS(DSA), .US(USA), .p2(p2), .running(running), .RESET(reset), .USP(us), .DSP(ds), .resC(tunnel));
  D_Flip_Flop #(.Pre_Clr_Positions("LEGACY"), .enable("true"), .NewFFLayout("false")) d_ff_2 (
    .clk(or_1_out), .D(not_3_out), .Q(B_JOGANDO), .Qn(d_ff_2_qn), .reset(reset));  // open: preset, en
  D_Flip_Flop #(.Pre_Clr_Positions("LEGACY"), .enable("true"), .NewFFLayout("false")) d_ff_3 (
    .clk(\situação_1_out_4 ), .D(CHUTANDO_X), .Q(CHUTANDO_Y), .Qn(d_ff_3_qn), .reset(reset));  // open: preset, en
  and and_12 (and_12_out, fim_temp_1_out_5, A_JOGANDO);
  and and_13 (and_13_out, fim_temp_2_out_5, B_JOGANDO);
  and and_14 (and_14_out, fim_temp_1_out_5, fim_temp_2_out_5);
  Button button_5 (.out(Iniciar));
  _7_Segment_Display u_7_segment_display_2 (
    .g(SX), .f(not_4_out), .a(not_4_out), .b(not_4_out), .e(not_4_out), .d(not_4_out), .c(not_4_out));  // open: dp
  and and_15 (A_JOGANDO, d_ff_2_qn, running);
  and and_16 (CHUTANDO_X, d_ff_3_qn, running);
  or or_2 (troca, and_12_out, and_13_out);
  or or_3 (or_3_out, and_14_out, pont_max_1_out_2, pont_max_2_out_2);
  and and_17 (Fim_de_jogo, or_3_out, running);
  Button button_6 (.out(PROXIMO));
  LED led_4 (.in(A_ganhou));
  LED led_5 (.in(menor));
  not not_4 (not_4_out, SX);
  Hex_Digit_Display hex_digit_display_7 (.value(XHC));  // open: dp
  LED led_6 (.in(CHUTANDO_X));
  or or_4 (dm, dma_t, dmb_t);
  LED led_7 (.in(tunnel));
  Button button_7 (.out(configurar));
  Button button_8 (.out(CHUTAR));
  LED led_8 (.in(Empate));
  LED led_9 (.in(Fim_de_jogo));
  LED led_10 (.in(acertou));
  LED led_11 (.in(igual));
  not not_5 (not_5_out, SY);
  _7_Segment_Display u_7_segment_display_3 (
    .g(SY), .f(not_5_out), .a(not_5_out), .b(not_5_out), .e(not_5_out), .d(not_5_out), .c(not_5_out));  // open: dp
  or or_5 (um, uma_t, umb_t);
  Nums_regra nums_regra_1 (.in_1({in_5, in_6, in_7, in_8}), .out_2(GA), .NEG(SA));
  Nums_regra nums_regra_2 (.in_1({in_1, in_2, in_3, in_4}), .out_2(GB), .NEG(SB));
  and and_18 (and_18_out, Iniciar, d_ff_4_qn);
  D_Flip_Flop #(.Pre_Clr_Positions("LEGACY"), .enable("true"), .NewFFLayout("false")) d_ff_4 (
    .clk(Iniciar), .D(Iniciar), .Qn(d_ff_4_qn), .reset(reset));  // open: Q, preset, en
  \time  time_2 (.in_1(acertou), .out_2(time_2_out_2));
  Button button_9 (.out(reset));
  LED led_12 (.in(B_ganhou));
  LED led_13 (.in(maior));
  Hex_Digit_Display hex_digit_display_8 (.value(YHC));  // open: dp
  LED led_14 (.in(CHUTANDO_Y));
  or or_6 (ds, dsa_t, dsb_t);
  Multiplexer #(.width(4), .enable("false")) multiplexer_1 (
    .in0(GA), .in1(GB), .out(multiplexer_1_out), .sel(B_JOGANDO));
  Multiplexer #(.enable("false")) multiplexer_2 (.in0(SA), .in1(SB), .out(multiplexer_2_out), .sel(B_JOGANDO));
  or or_7 (or_7_out, and_18_out, time_2_out_2);
  or or_8 (us, usa_t, usb_t);
  guard_chute guard_chute_1 (
    .A(CHUTANDO_X), .B(CHUTANDO_Y), .chutou(CHUTAR), .val_A(multiplexer_1_out), .SA(multiplexer_2_out),
    .reset(reset), .A_2(XHC), .B_2(YHC), .sinal_A(SX), .sinal_B(SY));
  Random #(.width(1)) random_1 (.clk(or_7_out), .next(or_7_out), .out(SVX));  // open: clr
  Random #(.width(3)) random_2 (.clk(or_7_out), .next(or_7_out), .out(random_2_out));  // open: clr
  debugger_random debugger_random_1 (.in_1(or_7_out), .out_2(debugger_random_1_out_2));
  Button button_10 (.out(dmb_t));
  Hex_Digit_Display hex_digit_display_9 (.value(DMB));  // open: dp
  Button button_11 (.out(umb_t));
  LED led_15 (.in(undriven_2));
  LED led_16 (.in(undriven_2));
  Hex_Digit_Display hex_digit_display_10 (.value(UMB));  // open: dp
  Hex_Digit_Display hex_digit_display_11 (.value(DSB));  // open: dp
  Hex_Digit_Display hex_digit_display_12 (.value(PB));  // open: dp
  not not_6 (not_6_out, SB);
  _7_Segment_Display u_7_segment_display_4 (
    .g(SB), .f(not_6_out), .a(not_6_out), .b(not_6_out), .e(not_6_out), .d(not_6_out), .c(not_6_out));  // open: dp
  Hex_Digit_Display hex_digit_display_13 (.value(GB));  // open: dp
  LED led_17 (.in(B_JOGANDO));
  cronometro_p2 cronometro_p2_1 (
    .START(p2), .DMP(dm), .UMP(um), .CONFIG(configurar), .running(running), .DM(DMB), .UM(UMB), .DS(DSB),
    .US(USB), .RESET(reset), .USP(us), .DSP(ds), .resC(tunnel));
  Random #(.width(1)) random_3 (.clk(debugger_random_1_out_2), .next(debugger_random_1_out_2), .out(SVY));  // open: clr
  Random #(.width(3)) random_4 (
    .clk(debugger_random_1_out_2), .next(debugger_random_1_out_2), .out(random_4_out));  // open: clr
  soma soma_1 (
    .in_1(1'b0), .in_2(1'b0), .in_3({1'b0, random_2_out}), .in_4({3'b000, SVX}), .out_7(ValX));  // open: s_plus, s_minus
  Button button_12 (.out(usb_t));
  Button button_13 (.out(dsb_t));
  Hex_Digit_Display hex_digit_display_14 (.value(USB));  // open: dp
  soma soma_2 (
    .in_1(SX), .in_2(SY), .in_3(XHC), .in_4(YHC), .s_minus(SValSomChute), .out_7(valSomChute));  // open: s_plus
  soma soma_3 (
    .in_1(SVX), .in_2(SVY), .in_3(ValX), .in_4(ValY), .s_minus(SValSomGuess), .out_7(valSomGuess));  // open: s_plus
  soma soma_4 (
    .in_1(1'b0), .in_2(1'b0), .in_3({1'b0, random_4_out}), .in_4({3'b000, SVY}), .out_7(ValY));  // open: s_plus, s_minus

  // Other names for the same wires on the sheet: A0 = in_8; A1 = in_7; A2 = in_6; A3 = in_5; B0 = in_4; B1 = in_3;
  //   B2 = in_2; B3 = in_1
endmodule

module pont_max (
  input  [3:0] in_1,
  output out_2
);

  magnitute magnitute_1 (.in_1(4'b1111), .in_2(in_1), .out_3(out_2));  // open: out_4, out_5
endmodule

module fim_temp (
  input  [3:0] in_1,
  input  [3:0] in_2,
  input  [3:0] in_3,
  input  [3:0] in_4,
  output out_5
);

  wire magnitute_1_out_3, magnitute_2_out_3, magnitute_3_out_3, magnitute_4_out_3;

  magnitute magnitute_1 (.in_1(4'b0000), .in_2(in_1), .out_3(magnitute_1_out_3));  // open: out_4, out_5
  magnitute magnitute_2 (.in_1(in_1), .in_2(in_2), .out_3(magnitute_2_out_3));  // open: out_4, out_5
  magnitute magnitute_3 (.in_1(in_3), .in_2(in_4), .out_3(magnitute_3_out_3));  // open: out_4, out_5
  magnitute magnitute_4 (.in_1(in_1), .in_2(in_4), .out_3(magnitute_4_out_3));  // open: out_4, out_5
  and and_1 (out_5, magnitute_1_out_3, magnitute_2_out_3, magnitute_3_out_3, magnitute_4_out_3);
endmodule

module incrementa (
  input  in_1,
  input  reset,
  output [3:0] out_3
);

  wire incrementador_1_s0, incrementador_1_s1, incrementador_1_s2, incrementador_1_s3;

  D_Flip_Flop #(.Pre_Clr_Positions("LEGACY"), .enable("true"), .NewFFLayout("false")) d_ff_1 (
    .clk(in_1), .D(incrementador_1_s3), .Q(out_3[3]), .reset(reset));  // open: Qn, preset, en
  D_Flip_Flop #(.Pre_Clr_Positions("LEGACY"), .enable("true"), .NewFFLayout("false")) d_ff_2 (
    .clk(in_1), .D(incrementador_1_s2), .Q(out_3[2]), .reset(reset));  // open: Qn, preset, en
  D_Flip_Flop #(.Pre_Clr_Positions("LEGACY"), .enable("true"), .NewFFLayout("false")) d_ff_3 (
    .clk(in_1), .D(incrementador_1_s1), .Q(out_3[1]), .reset(reset));  // open: Qn, preset, en
  incrementador incrementador_1 (
    .Q3(out_3[3]), .Q2(out_3[2]), .Q1(out_3[1]), .Q0(out_3[0]), .S3(incrementador_1_s3),
    .S2(incrementador_1_s2), .S1(incrementador_1_s1), .S0(incrementador_1_s0));
  D_Flip_Flop #(.Pre_Clr_Positions("LEGACY"), .enable("true"), .NewFFLayout("false")) d_ff_4 (
    .clk(in_1), .D(incrementador_1_s0), .Q(out_3[0]), .reset(reset));  // open: Qn, preset, en
endmodule

module incrementador (
  input  Q3,
  input  Q2,
  input  Q1,
  input  Q0,
  output S3,
  output S2,
  output S1,
  output S0
);

  wire and_1_out, and_2_out, and_3_out, and_4_out, and_5_out, and_6_out, not_1_out, not_2_out, not_3_out,
       not_4_out, not_5_out;

  and and_1 (and_1_out, Q2, Q1, Q0);
  not not_1 (not_1_out, Q2);
  and and_2 (and_2_out, not_1_out, Q1, Q0);
  and and_3 (and_3_out, Q2, not_2_out);
  not not_2 (not_2_out, Q1);
  and and_4 (and_4_out, Q2, not_3_out);
  not not_3 (not_3_out, Q0);
  not not_4 (not_4_out, Q1);
  and and_5 (and_5_out, not_4_out, Q0);
  and and_6 (and_6_out, Q1, not_5_out);
  not not_5 (not_5_out, Q0);
  not not_6 (S0, Q0);
  or or_1 (S3, and_1_out, Q3);
  or or_2 (S2, and_2_out, and_3_out, and_4_out);
  or or_3 (S1, and_5_out, and_6_out);
endmodule

module \situação  (
  input  in_1,
  input  in_2,
  output ok,
  output out_4
);

  wire and_1_out, and_2_out, d_ff_1_qn, d_ff_2_q;

  D_Flip_Flop #(.Pre_Clr_Positions("LEGACY"), .enable("true"), .NewFFLayout("false")) d_ff_1 (
    .clk(in_1), .D(d_ff_1_qn), .Q(ok), .Qn(d_ff_1_qn), .reset(and_2_out));  // open: preset, en
  D_Flip_Flop #(.Pre_Clr_Positions("LEGACY"), .enable("true"), .NewFFLayout("false")) d_ff_2 (
    .clk(in_1), .D(ok), .Q(d_ff_2_q), .reset(and_2_out));  // open: Qn, preset, en
  and and_1 (and_1_out, d_ff_2_q, in_2);
  and and_2 (and_2_out, in_1, ~in_2);  // AND_Gate
  or or_1 (out_4, and_1_out, and_2_out);
endmodule

module magnitute (
  input  [3:0] in_1,
  input  [3:0] in_2,
  output out_3,
  output out_4,
  output out_5
);

  wire and_1_out, and_2_out, and_3_out, and_4_out, xnor_1_out, xnor_2_out, xnor_3_out, xnor_4_out;

  xnor xnor_1 (xnor_1_out, in_1[0], in_2[0]);
  xnor xnor_2 (xnor_2_out, in_1[1], in_2[1]);
  xnor xnor_3 (xnor_3_out, in_2[2], in_1[2]);
  xnor xnor_4 (xnor_4_out, in_1[3], in_2[3]);
  and and_1 (and_1_out, in_1[3], ~in_2[3]);  // AND_Gate
  and and_2 (and_2_out, xnor_4_out, in_1[2], ~in_2[2]);  // AND_Gate
  and and_3 (and_3_out, xnor_3_out, xnor_4_out, in_1[1], ~in_2[1]);  // AND_Gate
  and and_4 (and_4_out, xnor_2_out, xnor_4_out, xnor_3_out, in_1[0], ~in_2[0]);  // AND_Gate
  and and_5 (out_3, xnor_1_out, xnor_2_out, xnor_3_out, xnor_4_out);
  or or_1 (out_4, and_1_out, and_2_out, and_3_out, and_4_out);
  and and_6 (out_5, ~out_4, ~out_3);  // AND_Gate
endmodule

module mag_inteiro (
  input  in_1,
  input  [3:0] in_2,
  input  in_3,
  input  [3:0] in_4,
  output Igual,
  output maior,
  output menor,
  output positivo,
  output negativo
);

  wire and_1_out, and_2_out, and_3_out, and_4_out, and_5_out, and_6_out, and_8_out, and_9_out, and_10_out,
       and_11_out, and_12_out, magnitute_1_out_3, magnitute_1_out_4, magnitute_1_out_5, xnor_1_out;

  magnitute magnitute_1 (
    .in_1(in_2), .in_2(in_4), .out_3(magnitute_1_out_3), .out_4(magnitute_1_out_4), .out_5(magnitute_1_out_5));
  xnor xnor_1 (xnor_1_out, in_1, in_3);
  and and_1 (and_1_out, magnitute_1_out_3, ~in_1, in_3);  // AND_Gate
  and and_2 (and_2_out, magnitute_1_out_4, ~in_1, in_3);  // AND_Gate
  and and_3 (and_3_out, magnitute_1_out_5, ~in_1, in_3);  // AND_Gate
  and and_4 (and_4_out, ~in_1, ~in_3, magnitute_1_out_4);  // AND_Gate
  and and_5 (and_5_out, in_1, in_3, magnitute_1_out_5);
  and and_6 (and_6_out, in_1, magnitute_1_out_5, in_3);
  and and_7 (Igual, xnor_1_out, magnitute_1_out_3);
  or or_1 (maior, and_1_out, and_2_out, and_3_out, and_4_out, and_5_out, and_6_out);
  and and_8 (and_8_out, ~in_1, ~in_3);  // AND_Gate
  and and_9 (and_9_out, ~in_1, magnitute_1_out_4, in_3);  // AND_Gate
  and and_10 (and_10_out, in_1, magnitute_1_out_5, ~in_3);  // AND_Gate
  and and_11 (and_11_out, magnitute_1_out_3, ~in_1, in_3);  // AND_Gate
  and and_12 (and_12_out, magnitute_1_out_3, ~in_3, in_1);  // AND_Gate
  and and_13 (menor, ~Igual, ~maior);  // AND_Gate
  or or_2 (positivo, and_8_out, and_9_out, and_10_out, and_11_out, and_12_out);
  not not_1 (negativo, positivo);
endmodule

module soma (
  input  in_1,
  input  in_2,
  input  [3:0] in_3,
  input  [3:0] in_4,
  output s_plus,
  output s_minus,
  output [3:0] out_7
);

  wire magnitute_1_out_5, not_1_out, somador_comp_1_co, somador_comp_2_co, somador_comp_3_co, xor_1_out,
       xor_2_out, xor_3_out, xor_4_out, xor_5_out;
  wire [3:0] multiplexer_1_out, multiplexer_2_out;

  xor xor_1 (xor_1_out, in_1, in_2);
  Multiplexer #(.width(4), .enable("false")) multiplexer_1 (
    .in0(in_3), .in1(in_4), .out(multiplexer_1_out), .sel(magnitute_1_out_5));
  magnitute magnitute_1 (.in_1(in_3), .in_2(in_4), .out_5(magnitute_1_out_5));  // open: out_3, out_4
  not not_1 (not_1_out, magnitute_1_out_5);
  Multiplexer #(.width(4), .enable("false")) multiplexer_2 (
    .in0(in_3), .in1(in_4), .out(multiplexer_2_out), .sel(not_1_out));
  xor xor_2 (xor_2_out, xor_1_out, multiplexer_2_out[0]);
  xor xor_3 (xor_3_out, xor_1_out, multiplexer_2_out[1]);
  xor xor_4 (xor_4_out, xor_1_out, multiplexer_2_out[2]);
  xor xor_5 (xor_5_out, xor_1_out, multiplexer_2_out[3]);
  mag_inteiro mag_inteiro_1 (
    .in_1(in_1), .in_2(in_3), .in_3(in_2), .in_4(in_4), .positivo(s_plus), .negativo(s_minus));  // open: Igual, maior, menor
  somador_comp somador_comp_1 (
    .ci(xor_1_out), .in_2(multiplexer_1_out[0]), .in_3(xor_2_out), .s(out_7[0]), .co(somador_comp_1_co));
  somador_comp somador_comp_2 (
    .ci(somador_comp_1_co), .in_2(multiplexer_1_out[1]), .in_3(xor_3_out), .s(out_7[1]),
    .co(somador_comp_2_co));
  somador_comp somador_comp_3 (
    .ci(somador_comp_2_co), .in_2(multiplexer_1_out[2]), .in_3(xor_4_out), .s(out_7[2]),
    .co(somador_comp_3_co));
  somador_comp somador_comp_4 (
    .ci(somador_comp_3_co), .in_2(multiplexer_1_out[3]), .in_3(xor_5_out), .s(out_7[3]));  // open: co
endmodule

module somador (
  input  in_1,
  input  in_2,
  output s,
  output out_4
);

  xor xor_1 (s, in_1, in_2);
  and and_1 (out_4, in_1, in_2);
endmodule

module somador_comp (
  input  ci,
  input  in_2,
  input  in_3,
  output s,
  output co
);

  wire somador_1_out_4, somador_1_s, somador_2_out_4;

  somador somador_1 (.in_1(in_2), .in_2(in_3), .s(somador_1_s), .out_4(somador_1_out_4));
  somador somador_2 (.in_1(ci), .in_2(somador_1_s), .s(s), .out_4(somador_2_out_4));
  or or_1 (co, somador_2_out_4, somador_1_out_4);
endmodule

module subtrator (
  input  ret1,
  input  V1,
  input  V2,
  output SA,
  output VA
);

  wire and_1_out;

  and and_1 (and_1_out, ~ret1, V1);  // AND_Gate
  and and_2 (SA, ~and_1_out, V2);  // AND_Gate
  xor xor_1 (VA, and_1_out, V2);
endmodule

module \time  (
  input  in_1,
  output out_2
);

  wire clock_1_out, d_ff_2_q, not_1_out;

  Clock clock_1 (.out(clock_1_out));
  D_Flip_Flop #(.Pre_Clr_Positions("LEGACY"), .enable("true"), .NewFFLayout("false")) d_ff_1 (
    .clk(not_1_out), .D(not_1_out), .Q(out_2), .reset(d_ff_2_q));  // open: Qn, preset, en
  not not_1 (not_1_out, in_1);
  D_Flip_Flop #(.Pre_Clr_Positions("LEGACY"), .enable("true"), .NewFFLayout("false")) d_ff_2 (
    .clk(clock_1_out), .D(out_2), .Q(d_ff_2_q));  // open: Qn, preset, en, reset
endmodule

module guard_chute (
  input  A,
  input  B,
  input  chutou,
  input  [3:0] val_A,
  input  SA,
  input  reset,
  output [3:0] A_2,
  output [3:0] B_2,
  output sinal_A,
  output sinal_B
);

  wire and_1_out, and_2_out, undriven;

  and and_1 (and_1_out, A, chutou);
  and and_2 (and_2_out, B, chutou);
  D_Flip_Flop #(.Pre_Clr_Positions("LEGACY"), .enable("true"), .NewFFLayout("false")) d_ff_1 (
    .clk(and_1_out), .D(val_A[3]), .Q(A_2[3]), .reset(reset));  // open: Qn, preset, en
  D_Flip_Flop #(.Pre_Clr_Positions("LEGACY"), .enable("true"), .NewFFLayout("false")) d_ff_2 (
    .clk(and_2_out), .D(val_A[3]), .Q(B_2[3]), .en(undriven), .reset(reset));  // open: Qn, preset
  D_Flip_Flop #(.Pre_Clr_Positions("LEGACY"), .enable("true"), .NewFFLayout("false")) d_ff_3 (
    .clk(and_1_out), .D(val_A[2]), .Q(A_2[2]), .reset(reset));  // open: Qn, preset, en
  D_Flip_Flop #(.Pre_Clr_Positions("LEGACY"), .enable("true"), .NewFFLayout("false")) d_ff_4 (
    .clk(and_2_out), .D(val_A[2]), .Q(B_2[2]), .reset(reset));  // open: Qn, preset, en
  D_Flip_Flop #(.Pre_Clr_Positions("LEGACY"), .enable("true"), .NewFFLayout("false")) d_ff_5 (
    .clk(and_1_out), .D(val_A[1]), .Q(A_2[1]), .reset(reset));  // open: Qn, preset, en
  D_Flip_Flop #(.Pre_Clr_Positions("LEGACY"), .enable("true"), .NewFFLayout("false")) d_ff_6 (
    .clk(and_2_out), .D(val_A[1]), .Q(B_2[1]), .reset(reset));  // open: Qn, preset, en
  D_Flip_Flop #(.Pre_Clr_Positions("LEGACY"), .enable("true"), .NewFFLayout("false")) d_ff_7 (
    .clk(and_1_out), .D(val_A[0]), .Q(A_2[0]), .reset(reset));  // open: Qn, preset, en
  D_Flip_Flop #(.Pre_Clr_Positions("LEGACY"), .enable("true"), .NewFFLayout("false")) d_ff_8 (
    .clk(and_2_out), .D(val_A[0]), .Q(B_2[0]), .reset(reset));  // open: Qn, preset, en
  D_Flip_Flop #(.Pre_Clr_Positions("LEGACY"), .enable("true"), .NewFFLayout("false")) d_ff_9 (
    .clk(and_1_out), .D(SA), .Q(sinal_A), .reset(reset));  // open: Qn, preset, en
  D_Flip_Flop #(.Pre_Clr_Positions("LEGACY"), .enable("true"), .NewFFLayout("false")) d_ff_10 (
    .clk(and_2_out), .D(SA), .Q(sinal_B), .reset(reset));  // open: Qn, preset, en
endmodule

module Nums_regra (
  input  [3:0] in_1,
  output [3:0] out_2,
  output NEG
);

  wire and_2_out, and_3_out, and_4_out, and_5_out, and_6_out, and_7_out, and_8_out, not_1_out, not_2_out,
       not_3_out, not_4_out, not_5_out, not_6_out, not_7_out, not_8_out, not_9_out, not_10_out, not_11_out;

  not not_1 (not_1_out, in_1[2]);
  not not_2 (not_2_out, in_1[1]);
  not not_3 (not_3_out, in_1[0]);
  not not_4 (not_4_out, in_1[3]);
  not not_5 (not_5_out, in_1[1]);
  not not_6 (not_6_out, in_1[0]);
  not not_7 (not_7_out, in_1[2]);
  not not_8 (not_8_out, in_1[2]);
  not not_9 (not_9_out, in_1[3]);
  not not_10 (not_10_out, in_1[0]);
  not not_11 (not_11_out, in_1[1]);
  and and_1 (out_2[3], in_1[3], not_1_out, not_2_out, not_3_out);
  and and_2 (and_2_out, not_4_out, in_1[2]);
  and and_3 (and_3_out, in_1[2], not_5_out, not_6_out);
  and and_4 (and_4_out, in_1[3], not_7_out, in_1[0]);
  and and_5 (and_5_out, in_1[3], not_8_out, in_1[1]);
  and and_6 (and_6_out, not_9_out, in_1[1]);
  and and_7 (and_7_out, in_1[1], not_10_out);
  and and_8 (and_8_out, in_1[3], not_11_out, in_1[0]);
  or or_1 (out_2[2], and_2_out, and_3_out, and_4_out, and_5_out);
  or or_2 (out_2[1], and_6_out, and_7_out, and_8_out);

  assign NEG = in_1[3];
  assign out_2[0] = in_1[0];
endmodule

module Ret_regra (
  input  NEG,
  input  [3:0] in_2,
  output [3:0] out_3
);

  wire and_1_out, and_2_out, and_3_out, and_4_out, and_5_out, and_6_out, and_7_out, and_8_out, and_9_out,
       and_10_out, not_1_out, not_2_out, not_3_out, not_4_out, not_5_out, not_6_out, not_7_out, not_8_out,
       not_9_out;

  not not_1 (not_1_out, NEG);
  not not_2 (not_2_out, in_2[1]);
  not not_3 (not_3_out, in_2[0]);
  not not_4 (not_4_out, in_2[3]);
  not not_5 (not_5_out, in_2[2]);
  not not_6 (not_6_out, NEG);
  not not_7 (not_7_out, in_2[0]);
  not not_8 (not_8_out, in_2[1]);
  not not_9 (not_9_out, in_2[3]);
  and and_1 (and_1_out, not_1_out, in_2[2]);
  and and_2 (and_2_out, in_2[2], not_2_out, not_3_out);
  and and_3 (and_3_out, NEG, not_4_out, not_5_out);
  and and_4 (and_4_out, not_6_out, in_2[1]);
  and and_5 (and_5_out, in_2[1], not_7_out);
  and and_6 (and_6_out, NEG, not_8_out, in_2[0]);
  and and_7 (and_7_out, not_9_out, in_2[0]);
  and and_8 (and_8_out, in_2[1], in_2[0]);
  and and_9 (and_9_out, in_2[2], in_2[0]);
  and and_10 (and_10_out, NEG, in_2[0]);
  or or_1 (out_3[2], and_1_out, and_2_out, and_3_out);
  or or_2 (out_3[1], and_4_out, and_5_out, and_6_out);
  or or_3 (out_3[0], and_7_out, and_8_out, and_9_out, and_10_out);

  assign out_3[3] = NEG;
endmodule

module cronometro_p1 (
  input  proximo,
  input  RESET,
  input  START,
  input  USP,
  input  DMP,
  input  DSP,
  input  UMP,
  input  CONFIG,
  output p2,
  output running,
  output [3:0] DM,
  output [3:0] UM,
  output [3:0] DS,
  output [3:0] US,
  output resC
);

  wire and_1_out, and_2_out, and_3_out, and_4_out, and_5_out, and_6_out, and_7_out, clock_1_out,
       crono_60_2_pulso, d_ff_3_q, fim_temp_1_out_5, not_1_out, not_2_out;

  not not_1 (not_1_out, p2);
  fim_temp fim_temp_1 (.in_1(DM), .in_2(UM), .in_3(DS), .in_4(US), .out_5(fim_temp_1_out_5));
  D_Flip_Flop #(.Pre_Clr_Positions("LEGACY"), .enable("true"), .NewFFLayout("false")) d_ff_1 (
    .clk(proximo), .D(not_1_out), .Q(p2), .reset(RESET));  // open: Qn, preset, en
  D_Flip_Flop #(.Pre_Clr_Positions("LEGACY"), .enable("true"), .NewFFLayout("false")) d_ff_2 (
    .clk(START), .D(START), .Q(running), .reset(RESET));  // open: Qn, preset, en
  and and_1 (and_1_out, ~p2, running);  // AND_Gate
  crono_60 crono_60_1 (
    .DS(DM), .US(UM), .reset(RESET), .on(and_1_out), .set_US(and_3_out), .set_DS(and_2_out),
    .CLK(crono_60_2_pulso));  // open: pulso
  and and_2 (and_2_out, resC, DMP);
  and and_3 (and_3_out, resC, UMP);
  and and_4 (and_4_out, ~fim_temp_1_out_5, and_5_out);  // AND_Gate
  and and_5 (and_5_out, ~resC, clock_1_out);  // AND_Gate
  D_Flip_Flop #(.Pre_Clr_Positions("LEGACY"), .enable("true"), .NewFFLayout("false")) d_ff_3 (
    .clk(CONFIG), .D(not_2_out), .Q(d_ff_3_q), .reset(RESET));  // open: Qn, preset, en
  not not_2 (not_2_out, d_ff_3_q);
  crono_60 crono_60_2 (
    .pulso(crono_60_2_pulso), .DS(DS), .US(US), .reset(RESET), .on(and_1_out), .set_US(and_6_out),
    .set_DS(and_7_out), .CLK(and_4_out));
  and and_6 (and_6_out, resC, USP);
  and and_7 (and_7_out, resC, DSP);
  Clock clock_1 (.out(clock_1_out));
  and and_8 (resC, ~running, d_ff_3_q);  // AND_Gate
endmodule

module cronometro_p2 (
  input  RESET,
  input  START,
  input  USP,
  input  DMP,
  input  DSP,
  input  UMP,
  input  CONFIG,
  input  running,
  output [3:0] DM,
  output [3:0] UM,
  output [3:0] DS,
  output [3:0] US,
  output resC
);

  wire and_1_out, and_2_out, and_3_out, and_4_out, and_5_out, and_6_out, clock_1_out, crono_60_2_pulso,
       d_ff_1_q, fim_temp_1_out_5, not_1_out, or_1_out;

  fim_temp fim_temp_1 (.in_1(DM), .in_2(UM), .in_3(DS), .in_4(US), .out_5(fim_temp_1_out_5));
  crono_60 crono_60_1 (
    .DS(DM), .US(UM), .reset(RESET), .on(START), .set_US(and_2_out), .set_DS(and_1_out),
    .CLK(crono_60_2_pulso));  // open: pulso
  and and_1 (and_1_out, d_ff_1_q, DMP);
  and and_2 (and_2_out, d_ff_1_q, UMP);
  not not_1 (not_1_out, d_ff_1_q);
  and and_3 (and_3_out, ~fim_temp_1_out_5, and_4_out);  // AND_Gate
  and and_4 (and_4_out, ~d_ff_1_q, clock_1_out);  // AND_Gate
  D_Flip_Flop #(.Pre_Clr_Positions("LEGACY"), .enable("true"), .NewFFLayout("false")) d_ff_1 (
    .clk(CONFIG), .D(not_1_out), .Q(d_ff_1_q), .reset(or_1_out));  // open: Qn, preset, en
  or or_1 (or_1_out, START, RESET);
  crono_60 crono_60_2 (
    .pulso(crono_60_2_pulso), .DS(DS), .US(US), .reset(RESET), .on(START), .set_US(and_5_out),
    .set_DS(and_6_out), .CLK(and_3_out));
  and and_5 (and_5_out, d_ff_1_q, USP);
  and and_6 (and_6_out, d_ff_1_q, DSP);
  Clock clock_1 (.out(clock_1_out));
  and and_7 (resC, ~running, d_ff_1_q);  // AND_Gate
endmodule

module crono_60 (
  input  reset,
  input  on,
  input  set_US,
  input  set_DS,
  input  CLK,
  output [3:0] DS,
  output [3:0] US,
  output pulso
);

  wire cont_reg_9_1_troca;

  Hex_Digit_Display hex_digit_display_1 (.value(DS));  // open: dp
  cont_reg_5 cont_reg_5_1 (
    .CLK(cont_reg_9_1_troca), .Set(set_DS), .Troca(pulso), .on_off(on), .Clear(reset), .\Saída_Num (DS));  // open: test
  Hex_Digit_Display hex_digit_display_2 (.value(US));  // open: dp
  cont_reg_9 cont_reg_9_1 (
    .CLK(CLK), .Set(set_US), .Troca(cont_reg_9_1_troca), .on_off(on), .Clear(reset), .\Saída_Num (US));  // open: test
endmodule

module cont_reg_9 (
  input  CLK,
  input  Set,
  input  on_off,
  input  Clear,
  output Troca,
  output [3:0] \Saída_Num ,
  output [3:0] test
);

  wire num_regra_9_reg_1_s0, num_regra_9_reg_1_s1, num_regra_9_reg_1_s2, num_regra_9_reg_1_s3, or_1_out,
       or_2_out;

  or or_1 (or_1_out, CLK, Set);
  or or_2 (or_2_out, Set, on_off);
  D_Flip_Flop #(.Pre_Clr_Positions("LEGACY"), .enable("true"), .NewFFLayout("false")) d_ff_1 (
    .clk(or_1_out), .D(num_regra_9_reg_1_s3), .Q(\Saída_Num [3]), .Qn(test[3]), .en(or_2_out), .reset(Clear));  // open: preset
  D_Flip_Flop #(.Pre_Clr_Positions("LEGACY"), .enable("true"), .NewFFLayout("false")) d_ff_2 (
    .clk(or_1_out), .D(num_regra_9_reg_1_s2), .Q(\Saída_Num [2]), .Qn(test[2]), .en(or_2_out), .reset(Clear));  // open: preset
  Num_regra_9_reg num_regra_9_reg_1 (
    .Q3(\Saída_Num [3]), .Q2(\Saída_Num [2]), .Q1(\Saída_Num [1]), .Q0(\Saída_Num [0]),
    .S3(num_regra_9_reg_1_s3), .S2(num_regra_9_reg_1_s2), .S1(num_regra_9_reg_1_s1), .Troca(Troca),
    .S0(num_regra_9_reg_1_s0));
  D_Flip_Flop #(.Pre_Clr_Positions("LEGACY"), .enable("true"), .NewFFLayout("false")) d_ff_3 (
    .clk(or_1_out), .D(num_regra_9_reg_1_s1), .Q(\Saída_Num [1]), .Qn(test[1]), .en(or_2_out), .reset(Clear));  // open: preset
  D_Flip_Flop #(.Pre_Clr_Positions("LEGACY"), .enable("true"), .NewFFLayout("false")) d_ff_4 (
    .clk(or_1_out), .D(num_regra_9_reg_1_s0), .Q(\Saída_Num [0]), .Qn(test[0]), .en(or_2_out), .reset(Clear));  // open: preset
  Hex_Digit_Display hex_digit_display_1 (.value(\Saída_Num ));  // open: dp
endmodule

module cont_reg_5 (
  input  CLK,
  input  Set,
  input  on_off,
  input  Clear,
  output Troca,
  output [3:0] \Saída_Num ,
  output [3:0] test
);

  wire num_regra_5_reg_1_s0, num_regra_5_reg_1_s1, num_regra_5_reg_1_s2, num_regra_5_reg_1_s3, or_1_out,
       or_2_out;

  or or_1 (or_1_out, CLK, Set);
  D_Flip_Flop #(.Pre_Clr_Positions("LEGACY"), .enable("true"), .NewFFLayout("false")) d_ff_1 (
    .clk(or_1_out), .D(num_regra_5_reg_1_s3), .Q(\Saída_Num [3]), .Qn(test[3]), .en(or_2_out), .reset(Clear));  // open: preset
  or or_2 (or_2_out, Set, on_off);
  D_Flip_Flop #(.Pre_Clr_Positions("LEGACY"), .enable("true"), .NewFFLayout("false")) d_ff_2 (
    .clk(or_1_out), .D(num_regra_5_reg_1_s2), .Q(\Saída_Num [2]), .Qn(test[2]), .en(or_2_out), .reset(Clear));  // open: preset
  Num_regra_5_reg num_regra_5_reg_1 (
    .Q0(\Saída_Num [3]), .Q1(\Saída_Num [2]), .Q2(\Saída_Num [1]), .Q3(\Saída_Num [0]),
    .S3(num_regra_5_reg_1_s3), .S2(num_regra_5_reg_1_s2), .S1(num_regra_5_reg_1_s1),
    .S0(num_regra_5_reg_1_s0), .Troca(Troca));
  D_Flip_Flop #(.Pre_Clr_Positions("LEGACY"), .enable("true"), .NewFFLayout("false")) d_ff_3 (
    .clk(or_1_out), .D(num_regra_5_reg_1_s1), .Q(\Saída_Num [1]), .Qn(test[1]), .en(or_2_out), .reset(Clear));  // open: preset
  D_Flip_Flop #(.Pre_Clr_Positions("LEGACY"), .enable("true"), .NewFFLayout("false")) d_ff_4 (
    .clk(or_1_out), .D(num_regra_5_reg_1_s0), .Q(\Saída_Num [0]), .Qn(test[0]), .en(or_2_out), .reset(Clear));  // open: preset
  Hex_Digit_Display hex_digit_display_1 (.value(\Saída_Num ));  // open: dp
endmodule

module Num_regra_9_reg (
  input  Q3,
  input  Q2,
  input  Q1,
  input  Q0,
  output S3,
  output S2,
  output S1,
  output Troca,
  output S0
);

  wire and_1_out, and_2_out, and_3_out, and_4_out, and_5_out, and_6_out, and_7_out, and_8_out, and_9_out,
       and_10_out, and_11_out, clock_1_out, d_ff_1_q;

  not not_1 (S0, Q0);
  and and_1 (and_1_out, ~Q3, ~Q2, ~Q1, ~Q0);  // AND_Gate
  and and_2 (and_2_out, Q3, Q0);
  and and_3 (and_3_out, Q3, Q1);
  and and_4 (and_4_out, Q2, Q0);
  and and_5 (and_5_out, Q2, Q1);
  and and_6 (and_6_out, Q3, ~Q1, ~Q0);  // AND_Gate
  and and_7 (and_7_out, Q1, Q0);
  and and_8 (and_8_out, Q2, ~Q1, ~Q0);  // AND_Gate
  and and_9 (and_9_out, Q3, ~Q1, ~Q0);  // AND_Gate
  or or_1 (S3, and_1_out, and_2_out, and_3_out);
  or or_2 (S2, and_4_out, and_5_out, and_6_out);
  or or_3 (S1, and_7_out, and_8_out, and_9_out);
  and and_10 (and_10_out, Q0, Q3);
  Clock clock_1 (.out(clock_1_out));
  and and_11 (and_11_out, S3, S0);
  D_Flip_Flop #(.Pre_Clr_Positions("LEGACY"), .enable("true"), .NewFFLayout("false")) d_ff_1 (
    .clk(clock_1_out), .D(and_11_out), .Q(d_ff_1_q));  // open: Qn, preset, en, reset
  and and_12 (Troca, and_10_out, d_ff_1_q);
endmodule

module Num_regra_5_reg (
  input  Q0,
  input  Q1,
  input  Q2,
  input  Q3,
  output S3,
  output S2,
  output S1,
  output S0,
  output Troca
);

  wire and_1_out, and_3_out, and_4_out, and_5_out, and_6_out, and_7_out, and_8_out, clock_1_out, d_ff_1_q,
       not_1_out, not_2_out, not_3_out, not_4_out, not_5_out, not_6_out;

  and and_1 (and_1_out, Q1, Q3);
  and and_2 (S3, Q0, Q2);
  not not_1 (not_1_out, Q1);
  not not_2 (not_2_out, Q2);
  not not_3 (not_3_out, Q3);
  not not_4 (not_4_out, Q0);
  not not_5 (not_5_out, Q3);
  not not_6 (not_6_out, Q3);
  and and_3 (and_3_out, Q0, Q2);
  and and_4 (and_4_out, not_1_out, not_2_out, not_3_out);
  and and_5 (and_5_out, not_4_out, Q1, Q3);
  and and_6 (and_6_out, Q2, Q3);
  and and_7 (and_7_out, Q1, not_5_out);
  or or_1 (S0, not_6_out, and_3_out);
  or or_2 (S2, and_4_out, and_5_out);
  or or_3 (S1, and_6_out, and_7_out, Q0);
  Clock clock_1 (.out(clock_1_out));
  and and_8 (and_8_out, S2, S0);
  D_Flip_Flop #(.Pre_Clr_Positions("LEGACY"), .enable("true"), .NewFFLayout("false")) d_ff_1 (
    .clk(clock_1_out), .D(and_8_out), .Q(d_ff_1_q));  // open: Qn, preset, en, reset
  and and_9 (Troca, d_ff_1_q, and_1_out);
endmodule

module debugger_random (
  input  in_1,
  output out_2
);

  wire time_1_out_2, time_2_out_2, time_3_out_2, time_4_out_2, time_5_out_2;

  \time  time_1 (.in_1(in_1), .out_2(time_1_out_2));
  \time  time_2 (.in_1(time_1_out_2), .out_2(time_2_out_2));
  \time  time_3 (.in_1(time_2_out_2), .out_2(time_3_out_2));
  \time  time_4 (.in_1(time_3_out_2), .out_2(time_4_out_2));
  \time  time_5 (.in_1(time_4_out_2), .out_2(time_5_out_2));
  or or_1 (out_2, time_5_out_2, time_1_out_2, time_3_out_2);
endmodule
